// Logisim project mini 8-bit computer.circ as structural Verilog: 21 circuits, main circuit main
module main (
);

  wire button_2_out, button_3_out, clk, clock_1_out, controlunit_1_alu_enout, controlunit_1_deco_eninxx,
       controlunit_1_deco_eninxy, controlunit_1_deco_ennum, controlunit_1_deco_enopc,
       controlunit_1_deco_load1, controlunit_1_deco_load2, controlunit_1_en_a, controlunit_1_en_b,
       controlunit_1_mem_enin, controlunit_1_mem_enout, controlunit_1_mem_setaddr, controlunit_1_pc_enout,
       controlunit_1_pc_inc, controlunit_1_pc_load, controlunit_1_pc_loadfromstack,
       controlunit_1_pc_setstack, controlunit_1_pc_stackdec, controlunit_1_pc_stackinc,
       controlunit_1_reg_enin, controlunit_1_reg_enout, controlunit_1_w_flag, decoder_1_format, rst;
  wire [2:0] alu_1_n, decoder_1_inx_x;
  wire [3:0] controlunit_1_alu_op, controlunit_1_joy_enout, decoder_1_opcode, joystick_1_x, joystick_1_y;
  wire [7:0] pc_1_pc_out;
  wire [14:0] monitor_control_1_out_8, monitor_control_1_out_9, monitor_control_1_out_10,
       monitor_control_1_out_11, monitor_control_1_out_12, monitor_control_1_out_13,
       monitor_control_1_out_14, monitor_control_1_out_15, monitor_control_1_out_16,
       monitor_control_1_out_17, monitor_control_1_out_18, monitor_control_1_out_19,
       monitor_control_1_out_20, monitor_control_1_out_21, monitor_control_1_out_22;

  Button button_1 (.out(rst));
  Button button_2 (.out(button_2_out));
  Clock clock_1 (.out(clock_1_out));
  PC pc_1 (
    .PC_load(controlunit_1_pc_load), .PC_in(pc_1_pc_out), .PC_inc(controlunit_1_pc_inc),
    .PC_out(pc_1_pc_out), .PC_enOut(controlunit_1_pc_enout), .PC_stackInc(controlunit_1_pc_stackinc),
    .PC_stackDec(controlunit_1_pc_stackdec), .PC_loadFromStack(controlunit_1_pc_loadfromstack),
    .PC_setStack(controlunit_1_pc_setstack), .clk(clk), .rst(rst));  // open: out_12
  or or_1 (clk, button_2_out, clock_1_out);
  ControlUnit controlunit_1 (
    .format(decoder_1_format), .opCode(decoder_1_opcode), .clk(clk), .rst(rst),
    .mem_setAddr(controlunit_1_mem_setaddr), .mem_enIn(controlunit_1_mem_enin),
    .mem_enOut(controlunit_1_mem_enout), .reg_enIn(controlunit_1_reg_enin),
    .reg_enOut(controlunit_1_reg_enout), .en_A(controlunit_1_en_a), .en_B(controlunit_1_en_b),
    .w_flag(controlunit_1_w_flag), .ALU_op(controlunit_1_alu_op), .ALU_enOut(controlunit_1_alu_enout),
    .CZN(alu_1_n), .mon_monSetLeast(controlunit_1_joy_enout[3]), .mon_setMost(controlunit_1_joy_enout[2]),
    .mon_enIn(controlunit_1_joy_enout[1]), .joy_enOut(controlunit_1_joy_enout[0]),
    .deco_load1(controlunit_1_deco_load1), .deco_load2(controlunit_1_deco_load2),
    .deco_enOpC(controlunit_1_deco_enopc), .deco_enInxX(controlunit_1_deco_eninxx),
    .deco_enInxY(controlunit_1_deco_eninxy), .deco_enNum(controlunit_1_deco_ennum),
    .PC_load(controlunit_1_pc_load), .PC_inc(controlunit_1_pc_inc), .PC_setStack(controlunit_1_pc_setstack),
    .PC_stackInc(controlunit_1_pc_stackinc), .PC_loadFromStack(controlunit_1_pc_loadfromstack),
    .PC_stackDec(controlunit_1_pc_stackdec), .PC_enOut(controlunit_1_pc_enout));
  Decoder decoder_1 (
    .clk(clk), .rst(rst), .deco_inst(pc_1_pc_out), .deco_enOpC(controlunit_1_deco_enopc),
    .deco_load1(controlunit_1_deco_load1), .deco_enInxY(controlunit_1_deco_eninxy),
    .deco_load2(controlunit_1_deco_load2), .deco_enNum(controlunit_1_deco_ennum), .opCode(decoder_1_opcode),
    .inx_X(decoder_1_inx_x), .inx_Y(decoder_1_inx_x), .num(pc_1_pc_out),
    .deco_enInxX(controlunit_1_deco_eninxx), .format(decoder_1_format));  // open: out_11, out_16
  monitor_control monitor_control_1 (
    .clk(clk), .rst(rst), .mon_setMost(controlunit_1_joy_enout[2]), .mon_halfIn(pc_1_pc_out),
    .mon_setLeast(controlunit_1_joy_enout[3]), .mon_inxCol(pc_1_pc_out[3:0]),
    .mon_enIn(controlunit_1_joy_enout[1]), .out_8(monitor_control_1_out_8), .out_9(monitor_control_1_out_9),
    .out_10(monitor_control_1_out_10), .out_11(monitor_control_1_out_11), .out_12(monitor_control_1_out_12),
    .out_13(monitor_control_1_out_13), .out_14(monitor_control_1_out_14), .out_15(monitor_control_1_out_15),
    .out_16(monitor_control_1_out_16), .out_17(monitor_control_1_out_17), .out_18(monitor_control_1_out_18),
    .out_19(monitor_control_1_out_19), .out_20(monitor_control_1_out_20), .out_21(monitor_control_1_out_21),
    .out_22(monitor_control_1_out_22));
  DotMatrix #(.matrixcols(15), .matrixrows(15)) dotmatrix_1 (
    .col0(monitor_control_1_out_8), .col1(monitor_control_1_out_9), .col2(monitor_control_1_out_10),
    .col3(monitor_control_1_out_11), .col4(monitor_control_1_out_12), .col5(monitor_control_1_out_13),
    .col6(monitor_control_1_out_14), .col7(monitor_control_1_out_15), .col8(monitor_control_1_out_16),
    .col9(monitor_control_1_out_17), .col10(monitor_control_1_out_18), .col11(monitor_control_1_out_19),
    .col12(monitor_control_1_out_20), .col13(monitor_control_1_out_21), .col14(monitor_control_1_out_22));
  Joystick joystick_1 (.x(joystick_1_x), .y(joystick_1_y));
  joystick_control joystick_control_1 (
    .joy_in({joystick_1_x, joystick_1_y}), .joy_enOut(controlunit_1_joy_enout[0]), .joy_out(pc_1_pc_out));
  ALU alu_1 (
    .clk(clk), .w_flag(controlunit_1_w_flag), .in_A(pc_1_pc_out), .en_A(controlunit_1_en_a),
    .in_B(pc_1_pc_out), .en_B(controlunit_1_en_b), .ALU_enOut(controlunit_1_alu_enout),
    .ALU_op(controlunit_1_alu_op), .C(alu_1_n[2]), .Z(alu_1_n[1]), .N(alu_1_n[0]), .ALU_out(pc_1_pc_out),
    .rst(rst));  // open: view_A, view_B
  Button button_3 (.out(button_3_out));
  Registers registers_1 (
    .reg_enIn(controlunit_1_reg_enin), .reg_inxIn(decoder_1_inx_x), .clk(clk), .rst(rst),
    .reg_out(pc_1_pc_out), .en_Out(controlunit_1_reg_enout), .inx_Out(decoder_1_inx_x), .reg_in(pc_1_pc_out));  // open: Reg_5_8, Reg_1_4
  Memory memory_1 (
    .mem_addr(pc_1_pc_out), .mem_in(pc_1_pc_out), .mem_enOut(controlunit_1_mem_enout),
    .mem_enIn(controlunit_1_mem_enin), .clk(clk), .clr(rst), .mem_out(pc_1_pc_out),
    .mem_setAddr(controlunit_1_mem_setaddr), .in_4(button_3_out));  // open: out_9
endmodule

module _1_bit_half_adder (
  input  in_A,
  input  in_B,
  output out,
  output c_out
);

  xor xor_1 (out, in_A, in_B);
  and and_1 (c_out, in_A, in_B);
endmodule

module _1_bit_full_adder (
  input  c_in,
  input  in_A,
  input  in_B,
  output out,
  output c_out
);

  wire n1_bit_half_adder_1_c_out, n1_bit_half_adder_2_c_out, n1_bit_half_adder_2_out;

  _1_bit_half_adder u_1_bit_half_adder_1 (
    .in_A(c_in), .in_B(n1_bit_half_adder_2_out), .c_out(n1_bit_half_adder_1_c_out), .out(out));
  _1_bit_half_adder u_1_bit_half_adder_2 (
    .in_A(in_A), .in_B(in_B), .c_out(n1_bit_half_adder_2_c_out), .out(n1_bit_half_adder_2_out));
  or or_1 (c_out, n1_bit_half_adder_1_c_out, n1_bit_half_adder_2_c_out);
endmodule

module _8_bit_adder (
  input  [7:0] in_A,
  input  [7:0] in_B,
  output [7:0] out,
  output c_out
);

  wire n1_bit_full_adder_1_c_out, n1_bit_full_adder_2_c_out, n1_bit_full_adder_3_c_out,
       n1_bit_full_adder_4_c_out, n1_bit_full_adder_5_c_out, n1_bit_full_adder_6_c_out,
       n1_bit_half_adder_1_c_out;

  _1_bit_half_adder u_1_bit_half_adder_1 (
    .in_A(in_A[0]), .in_B(in_B[0]), .c_out(n1_bit_half_adder_1_c_out), .out(out[0]));
  _1_bit_full_adder u_1_bit_full_adder_1 (
    .in_A(in_A[1]), .in_B(in_B[1]), .out(out[1]), .c_out(n1_bit_full_adder_1_c_out),
    .c_in(n1_bit_half_adder_1_c_out));
  _1_bit_full_adder u_1_bit_full_adder_2 (
    .in_A(in_A[2]), .in_B(in_B[2]), .out(out[2]), .c_out(n1_bit_full_adder_2_c_out),
    .c_in(n1_bit_full_adder_1_c_out));
  _1_bit_full_adder u_1_bit_full_adder_3 (
    .in_A(in_A[3]), .in_B(in_B[3]), .out(out[3]), .c_out(n1_bit_full_adder_3_c_out),
    .c_in(n1_bit_full_adder_2_c_out));
  _1_bit_full_adder u_1_bit_full_adder_4 (
    .in_A(in_A[4]), .in_B(in_B[4]), .out(out[4]), .c_out(n1_bit_full_adder_4_c_out),
    .c_in(n1_bit_full_adder_3_c_out));
  _1_bit_full_adder u_1_bit_full_adder_5 (
    .in_A(in_A[5]), .in_B(in_B[5]), .out(out[5]), .c_out(n1_bit_full_adder_5_c_out),
    .c_in(n1_bit_full_adder_4_c_out));
  _1_bit_full_adder u_1_bit_full_adder_6 (
    .in_A(in_A[6]), .in_B(in_B[6]), .out(out[6]), .c_out(n1_bit_full_adder_6_c_out),
    .c_in(n1_bit_full_adder_5_c_out));
  _1_bit_full_adder u_1_bit_full_adder_7 (
    .in_A(in_A[7]), .in_B(in_B[7]), .out(out[7]), .c_out(c_out), .c_in(n1_bit_full_adder_6_c_out));
endmodule

module _8_bit_negator (
  input  [7:0] in,
  output [7:0] out
);

  wire [7:0] xor_1_out;

  _8_bit_adder u_8_bit_adder_1 (.in_A(8'h1), .in_B(xor_1_out), .out(out));  // open: c_out
  assign xor_1_out = {8{1'b1}} ^ in;  // XOR_Gate xor_1, 8 bits wide
endmodule

module _8_bit_full_substractor (
  input  [7:0] in_A,
  input  [7:0] in_B,
  output [7:0] out,
  output b_out
);

  wire n8_bit_adder_1_c_out, nor_1_out, not_1_out;
  wire [7:0] n8_bit_negator_1_out;

  _8_bit_negator u_8_bit_negator_1 (.in(in_B), .out(n8_bit_negator_1_out));
  _8_bit_adder u_8_bit_adder_1 (.in_A(in_A), .in_B(n8_bit_negator_1_out), .out(out), .c_out(n8_bit_adder_1_c_out));
  nor nor_1 (nor_1_out, in_B[0], in_B[1], in_B[2], in_B[3], in_B[4], in_B[5], in_B[6], in_B[7]);
  not not_1 (not_1_out, n8_bit_adder_1_c_out);
  xor xor_1 (b_out, not_1_out, nor_1_out);
endmodule

module bit_shifter__left (
  input  [7:0] in_Value,
  input  [2:0] in_shift,
  output [7:0] out
);

  Multiplexer #(.select(3), .width(8)) multiplexer_1 (
    .in0(in_Value), .in1({in_Value[6:0], 1'b0}), .in2({in_Value[5:0], 2'b00}), .in3({in_Value[4:0], 3'b000}),
    .in4({in_Value[3:0], 4'b0000}), .in5({in_Value[2:0], {5{1'b0}}}), .in6({in_Value[1:0], {6{1'b0}}}),
    .in7({in_Value[0], {7{1'b0}}}), .out(out), .sel(in_shift));  // open: en
endmodule

module bit_shifter__right (
  input  [7:0] in_Value,
  input  [2:0] in_shift,
  output [7:0] out
);

  Multiplexer #(.select(3), .width(8)) multiplexer_1 (
    .in0(in_Value), .in1({1'b0, in_Value[7:1]}), .in2({2'b00, in_Value[7:2]}), .in3({3'b000, in_Value[7:3]}),
    .in4({4'b0000, in_Value[7:4]}), .in5({{5{1'b0}}, in_Value[7:5]}), .in6({{6{1'b0}}, in_Value[7:6]}),
    .in7({{7{1'b0}}, in_Value[7]}), .out(out), .sel(in_shift));  // open: en
endmodule

module _8_bit_incrementer (
  input  [7:0] in,
  output [7:0] out,
  output c_out
);

  _8_bit_adder u_8_bit_adder_1 (.in_A(in), .in_B(8'h1), .out(out), .c_out(c_out));
endmodule

module _8_bit_decrementer (
  input  [7:0] in,
  output [7:0] out,
  output b_out
);

  _8_bit_full_substractor u_8_bit_full_substractor_1 (.in_A(in), .in_B(8'h1), .out(out), .b_out(b_out));
endmodule

module _8_bit_to_3_bit_cutter (
  input  [7:0] in,
  output [2:0] out
);


  assign out = in[2:0];
endmodule

module D_flip_flop (
  input  D,
  input  clk,
  output Q
);

  wire and_1_out, and_2_out, nor_1_out, not_1_out;

  not not_1 (not_1_out, D);
  and and_1 (and_1_out, D, clk);
  and and_2 (and_2_out, clk, not_1_out);
  nor nor_1 (nor_1_out, and_1_out, Q);
  nor nor_2 (Q, nor_1_out, and_2_out);
endmodule

module _8_bit_Register (
  input  [7:0] In,
  input  clk,
  output [7:0] Out
);

  D_flip_flop d_flip_flop_1 (.D(In[0]), .clk(clk), .Q(Out[0]));
  D_flip_flop d_flip_flop_2 (.D(In[1]), .clk(clk), .Q(Out[1]));
  D_flip_flop d_flip_flop_3 (.D(In[2]), .clk(clk), .Q(Out[2]));
  D_flip_flop d_flip_flop_4 (.D(In[3]), .clk(clk), .Q(Out[3]));
  D_flip_flop d_flip_flop_5 (.D(In[4]), .clk(clk), .Q(Out[4]));
  D_flip_flop d_flip_flop_6 (.D(In[5]), .clk(clk), .Q(Out[5]));
  D_flip_flop d_flip_flop_7 (.D(In[6]), .clk(clk), .Q(Out[6]));
  D_flip_flop d_flip_flop_8 (.D(In[7]), .clk(clk), .Q(Out[7]));
endmodule

module ALU (
  input  clk,
  input  rst,
  input  w_flag,
  input  [7:0] in_A,
  input  en_A,
  input  [7:0] in_B,
  input  en_B,
  input  ALU_enOut,
  input  [3:0] ALU_op,
  output C,
  output Z,
  output N,
  output [7:0] ALU_out,
  output [7:0] view_A,
  output [7:0] view_B
);

  wire and_2_out, multiplexer_1_out, n8_bit_adder_1_c_out, n8_bit_decrementer_1_b_out,
       n8_bit_full_substractor_1_b_out, n8_bit_incrementer_1_c_out, nor_1_out, nor_2_out, not_1_out;
  wire [2:0] n8_bit_to_3_bit_cutter_1_out, n8_bit_to_3_bit_cutter_2_out;
  wire [7:0] and_1_out, bit_shifter_left_1_out, bit_shifter_right_1_out, multiplexer_2_out,
       n8_bit_adder_1_out, n8_bit_decrementer_1_out, n8_bit_full_substractor_1_out, n8_bit_incrementer_1_out,
       or_1_out, register_6_q, xor_1_out;

  Register register_1 (.D(in_A), .en(en_A), .Q(view_A), .clk(clk), .clr(rst));
  Register register_2 (.D(in_B), .en(en_B), .Q(view_B), .clk(clk), .clr(rst));
  _8_bit_adder u_8_bit_adder_1 (.in_A(view_A), .in_B(view_B), .out(n8_bit_adder_1_out), .c_out(n8_bit_adder_1_c_out));
  _8_bit_full_substractor u_8_bit_full_substractor_1 (
    .in_A(view_A), .in_B(view_B), .out(n8_bit_full_substractor_1_out), .b_out(n8_bit_full_substractor_1_b_out));
  _8_bit_incrementer u_8_bit_incrementer_1 (
    .in(view_A), .out(n8_bit_incrementer_1_out), .c_out(n8_bit_incrementer_1_c_out));
  _8_bit_decrementer u_8_bit_decrementer_1 (
    .in(view_A), .out(n8_bit_decrementer_1_out), .b_out(n8_bit_decrementer_1_b_out));
  bit_shifter__right bit_shifter_right_1 (
    .in_Value(view_A), .in_shift(n8_bit_to_3_bit_cutter_1_out), .out(bit_shifter_right_1_out));
  _8_bit_to_3_bit_cutter u_8_bit_to_3_bit_cutter_1 (.in(view_B), .out(n8_bit_to_3_bit_cutter_1_out));
  bit_shifter__left bit_shifter_left_1 (
    .in_Value(view_A), .in_shift(n8_bit_to_3_bit_cutter_2_out), .out(bit_shifter_left_1_out));
  _8_bit_to_3_bit_cutter u_8_bit_to_3_bit_cutter_2 (.in(view_B), .out(n8_bit_to_3_bit_cutter_2_out));
  assign or_1_out = view_A | view_B;  // OR_Gate or_1, 8 bits wide
  assign xor_1_out = view_A ^ view_B;  // XOR_Gate xor_1, 8 bits wide
  assign and_1_out = view_A & view_B;  // AND_Gate and_1, 8 bits wide
  Multiplexer #(.select(2)) multiplexer_1 (
    .in0(n8_bit_decrementer_1_b_out), .in1(n8_bit_adder_1_c_out), .in2(n8_bit_full_substractor_1_b_out),
    .in3(n8_bit_incrementer_1_c_out), .out(multiplexer_1_out), .sel(ALU_op[1:0]));  // open: en
  nor nor_1 (nor_1_out, ALU_op[2], ALU_op[3]);
  Multiplexer #(.select(4), .width(8)) multiplexer_2 (
    .in1(n8_bit_adder_1_out), .in2(n8_bit_full_substractor_1_out), .in3(n8_bit_incrementer_1_out),
    .in4(n8_bit_decrementer_1_out), .in5(bit_shifter_right_1_out), .in6(bit_shifter_left_1_out),
    .in7(or_1_out), .in8(xor_1_out), .in9(and_1_out), .in10({8{1'b0}}), .in11(8'h1), .in12(8'h2),
    .in13({8{1'b1}}), .out(multiplexer_2_out), .sel(ALU_op));  // open: in0, in14, in15, en
  and and_2 (and_2_out, multiplexer_1_out, nor_1_out);
  nor nor_2 (nor_2_out, multiplexer_2_out[0], multiplexer_2_out[1], multiplexer_2_out[2], multiplexer_2_out[3], multiplexer_2_out[4], multiplexer_2_out[5], multiplexer_2_out[6], multiplexer_2_out[7]);
  Register #(.width(1)) register_3 (.D(and_2_out), .en(w_flag), .Q(C), .clk(clk), .clr(rst));
  Register #(.width(1)) register_4 (.D(nor_2_out), .en(w_flag), .Q(Z), .clk(clk), .clr(rst));
  Register #(.width(1)) register_5 (.D(multiplexer_2_out[7]), .en(w_flag), .Q(N), .clk(clk), .clr(rst));
  Register register_6 (.D(multiplexer_2_out), .en(1'b1), .Q(register_6_q), .clk(not_1_out), .clr(rst));
  not not_1 (not_1_out, clk);
  assign ALU_out = ALU_enOut ? register_6_q : 8'bz;  // Controlled_Buffer controlled_buffer_1

  // Notes on the sheet:
  //   cte00 = 1010
  //   cte01 = 1011
  //   cte02 = 1100
  //   cteff = 1101
  //   ADD = 0001
  //   SUB = 0010
  //   INC = 0011
  //   DEC = 0100
  //   SHR = 0101
  //   SHL = 0110
  //   OR = 0111
  //   XOR = 1000
  //   AND = 1001
  //   C
  //   Z
  //   N
endmodule

// in_Reg
module Registers (
  input  [7:0] reg_in,
  input  reg_enIn,
  input  en_Out,
  input  [2:0] reg_inxIn,
  input  [2:0] inx_Out,
  input  clk,
  input  rst,
  output [31:0] Reg_1_4,
  output [7:0] reg_out,
  output [31:0] Reg_5_8
);

  wire decoder_1_out0, decoder_1_out1, decoder_1_out2, decoder_1_out3, decoder_1_out4, decoder_1_out5,
       decoder_1_out6, decoder_1_out7;

  Decoder_part #(.select(3), .disabled(0)) decoder_1 (
    .out0(decoder_1_out0), .out1(decoder_1_out1), .out2(decoder_1_out2), .out3(decoder_1_out3),
    .out4(decoder_1_out4), .out5(decoder_1_out5), .out6(decoder_1_out6), .out7(decoder_1_out7),
    .sel(reg_inxIn), .en(reg_enIn));
  Register register_1 (.D(reg_in), .en(decoder_1_out0), .Q(Reg_1_4[31:24]), .clk(clk), .clr(rst));
  Register register_2 (.D(reg_in), .en(decoder_1_out1), .Q(Reg_1_4[23:16]), .clk(clk), .clr(rst));
  Register register_3 (.D(reg_in), .en(decoder_1_out2), .Q(Reg_1_4[15:8]), .clk(clk), .clr(rst));
  Register register_4 (.D(reg_in), .en(decoder_1_out3), .Q(Reg_1_4[7:0]), .clk(clk), .clr(rst));
  Register register_5 (.D(reg_in), .en(decoder_1_out4), .Q(Reg_5_8[31:24]), .clk(clk), .clr(rst));
  Register register_6 (.D(reg_in), .en(decoder_1_out5), .Q(Reg_5_8[23:16]), .clk(clk), .clr(rst));
  Register register_7 (.D(reg_in), .en(decoder_1_out6), .Q(Reg_5_8[15:8]), .clk(clk), .clr(rst));
  Register register_8 (.D(reg_in), .en(decoder_1_out7), .Q(Reg_5_8[7:0]), .clk(clk), .clr(rst));
  Multiplexer #(.select(3), .width(8)) multiplexer_1 (
    .in0(Reg_1_4[31:24]), .in1(Reg_1_4[23:16]), .in2(Reg_1_4[15:8]), .in3(Reg_1_4[7:0]),
    .in4(Reg_5_8[31:24]), .in5(Reg_5_8[23:16]), .in6(Reg_5_8[15:8]), .in7(Reg_5_8[7:0]), .out(reg_out),
    .sel(inx_Out), .en(en_Out));
endmodule

module Memory (
  input  [7:0] mem_addr,
  input  mem_setAddr,
  input  [7:0] mem_in,
  input  in_4,
  input  mem_enOut,
  input  mem_enIn,
  input  clk,
  input  clr,
  output [7:0] out_9,
  output [7:0] mem_out
);

  wire [7:0] register_1_q;

  Register register_1 (.D(mem_addr), .en(mem_setAddr), .Q(register_1_q), .clk(clk), .clr(clr));
  RAM #(.bus("separate")) ram_1 (
    .addr(register_1_q), .din(mem_in), .data(out_9), .str(mem_enIn), .clk(clk), .clr(in_4));  // open: sel, ld
  assign mem_out = mem_enOut ? out_9 : 8'bz;  // Controlled_Buffer controlled_buffer_1

  // Other names for the same wires on the sheet: rst = clr
endmodule

module PC (
  input  clk,
  input  rst,
  input  PC_stackDec,
  input  PC_stackInc,
  input  PC_setStack,
  input  PC_loadFromStack,
  input  PC_load,
  input  [7:0] PC_in,
  input  PC_inc,
  input  PC_enOut,
  output [7:0] PC_out,
  output [7:0] out_12
);

  wire or_1_out;
  wire [3:0] counter_1_q;

  or or_1 (or_1_out, PC_stackDec, PC_stackInc);
  Counter #(.width(4), .max('hf)) counter_1 (
    .load(PC_stackDec), .count(or_1_out), .Q(counter_1_q), .clk(clk), .clr(rst));  // open: D, carry
  Counter counter_2 (.load(PC_load), .D(PC_in), .count(PC_inc), .Q(out_12), .clk(clk), .clr(rst));  // open: carry
  RAM #(.addrWidth(4), .bus("separate")) ram_1 (
    .addr(counter_1_q), .din(out_12), .data(PC_in), .str(PC_setStack), .clk(clk), .ld(PC_loadFromStack),
    .clr(rst));  // open: sel
  assign PC_out = PC_enOut ? out_12 : 8'bz;  // Controlled_Buffer controlled_buffer_1

  // Other names for the same wires on the sheet: PC_fromStack[7:0] = PC_in
endmodule

module Decoder (
  input  clk,
  input  rst,
  input  [7:0] deco_inst,
  input  deco_enOpC,
  input  deco_load1,
  input  deco_enInxX,
  input  deco_enInxY,
  input  deco_load2,
  input  deco_enNum,
  output format,
  output [3:0] out_11,
  output [3:0] opCode,
  output [2:0] inx_X,
  output [2:0] inx_Y,
  output [7:0] num,
  output [7:0] out_16
);

  wire [2:0] register_1_q;

  Register register_1 (.D(deco_inst), .en(deco_load1), .Q({out_11, format, register_1_q}), .clk(clk), .clr(rst));
  Register register_2 (.D(deco_inst), .en(deco_load2), .Q(out_16), .clk(clk), .clr(rst));
  assign opCode = deco_enOpC ? out_11 : 4'bz;  // Controlled_Buffer controlled_buffer_1
  assign inx_X = deco_enInxX ? register_1_q : 3'bz;  // Controlled_Buffer controlled_buffer_2
  assign inx_Y = deco_enInxY ? out_16[7:5] : 3'bz;  // Controlled_Buffer controlled_buffer_3
  assign num = deco_enNum ? out_16 : 8'bz;  // Controlled_Buffer controlled_buffer_4
endmodule

module ControlUnit (
  input  [2:0] CZN,
  input  format,
  input  [3:0] opCode,
  input  clk,
  input  rst,
  output PC_load,
  output PC_inc,
  output PC_setStack,
  output PC_stackInc,
  output PC_loadFromStack,
  output PC_stackDec,
  output PC_enOut,
  output deco_load1,
  output deco_load2,
  output deco_enOpC,
  output deco_enInxX,
  output deco_enInxY,
  output deco_enNum,
  output mem_setAddr,
  output mem_enIn,
  output mem_enOut,
  output reg_enIn,
  output reg_enOut,
  output en_A,
  output en_B,
  output w_flag,
  output [3:0] ALU_op,
  output ALU_enOut,
  output mon_setMost,
  output mon_monSetLeast,
  output mon_enIn,
  output joy_enOut
);

  wire and_1_out, and_2_out, and_3_out, and_4_out, decoder_1_out0, decoder_1_out1, decoder_1_out2, not_1_out,
       or_1_out;
  wire [0:0] or_2_out;
  wire [7:0] counter_1_q, n8_bit_adder_1_out;
  wire [31:30] rom_1_data;

  Decoder_part #(.select(2), .disabled(0)) decoder_1 (
    .out0(decoder_1_out0), .out1(decoder_1_out1), .out2(decoder_1_out2), .sel({opCode[0], format}),
    .en(and_1_out));  // open: out3
  and and_1 (and_1_out, opCode[3], opCode[2], ~opCode[1]);  // AND_Gate
  _8_bit_adder u_8_bit_adder_1 (
    .in_A({opCode, format, 3'b000}), .in_B({{7{1'b0}}, or_2_out[0]}), .out(n8_bit_adder_1_out));  // open: c_out
  not not_1 (not_1_out, rom_1_data[30]);
  or or_1 (or_1_out, rst, rom_1_data[31]);
  and and_2 (and_2_out, CZN[2], decoder_1_out0);
  and and_3 (and_3_out, CZN[1], decoder_1_out1);
  and and_4 (and_4_out, CZN[0], decoder_1_out2);
  or or_2 (or_2_out[0], and_4_out, and_3_out, and_2_out);
  Counter counter_1 (
    .load(rom_1_data[30]), .D(n8_bit_adder_1_out), .count(not_1_out), .Q(counter_1_q), .clk(clk),
    .clr(or_1_out));  // open: carry
  ROM #(.dataWidth(32)) rom_1 (
    .addr(counter_1_q),
    .data({rom_1_data, joy_enOut, mon_enIn, mon_monSetLeast, mon_setMost, ALU_enOut, ALU_op, w_flag, en_B, en_A, reg_enOut, reg_enIn, mem_enOut, mem_enIn, mem_setAddr, deco_enNum, deco_enInxY, deco_enInxX, deco_enOpC, deco_load2, deco_load1, PC_enOut, PC_stackDec, PC_loadFromStack, PC_stackInc, PC_setStack, PC_inc, PC_load}));  // open: sel

  // Notes on the sheet:
  //   CU_reset
  //   CU_load
  //   contents of rom_1 (hex, n*v repeats v):
  //   2040 8082 2040 8102 40000200 80000000 10*0 60400 a0800 300000 2010400 80000000 0 0 0 60400 81000
  //   300000 2010400 80000000 0 0 0 60400 a0800 500000 2010400 80000000 0 0 0 60400 81000 500000 2010400
  //   80000000 0 0 0 60400 2010400 80000000 5*0 60400 81000 2010400 80000000 4*0 60400 a0800 a00000
  //   2010400 80000000 0 0 0 60400 81000 a00000 2010400 80000000 0 0 0 60400 a0800 c00000 2010400 80000000
  //   0 0 0 60400 81000 c00000 2010400 80000000 0 0 0 60400 a0800 f00000 2010400 80000000 0 0 0 60400
  //   81000 f00000 2010400 80000000 0 0 0 60400 a0800 1f00000 2010400 80000000 0 0 0 60400 81000 1f00000
  //   2010400 80000000 0 0 0 60400 a0800 1300000 2010400 80000000 0 0 0 60400 81000 1300000 2010400
  //   80000000 0 0 0 60400 a0800 500000 80000000 4*0 60400 81000 500000 80000000 4*0 60400 3480000 2210800
  //   80000000 4*0 11400 80000000 6*0 3000 24400 80000000 5*0 3000 18400 80000000 5*0 80000000 1001
  //   80000000 5*0 80000000 1001 80000000 5*0 80000000 1001 80000000 5*0 1001 80000000 6*0 4 8 1001
  //   80000000 4*0 20 11 80000000 5*0 43000 8608000 2042000 4608000 2002000 10008000 80000000 0 3000
  //   20004000 80000000
endmodule

module monitor_control (
  input  clk,
  input  rst,
  input  mon_setMost,
  input  [7:0] mon_halfIn,
  input  mon_setLeast,
  input  [3:0] mon_inxCol,
  input  mon_enIn,
  output [14:0] out_8,
  output [14:0] out_9,
  output [14:0] out_10,
  output [14:0] out_11,
  output [14:0] out_12,
  output [14:0] out_13,
  output [14:0] out_14,
  output [14:0] out_15,
  output [14:0] out_16,
  output [14:0] out_17,
  output [14:0] out_18,
  output [14:0] out_19,
  output [14:0] out_20,
  output [14:0] out_21,
  output [14:0] out_22
);

  wire decoder_1_out1, decoder_1_out2, decoder_1_out3, decoder_1_out4, decoder_1_out5, decoder_1_out6,
       decoder_1_out7, decoder_1_out8, decoder_1_out9, decoder_1_out10, decoder_1_out11, decoder_1_out12,
       decoder_1_out13, decoder_1_out14, decoder_1_out15;
  wire [7:0] register_1_q, register_2_q;

  Register register_1 (.D(mon_halfIn), .en(mon_setMost), .Q(register_1_q), .clk(clk), .clr(rst));
  Register register_2 (.D(mon_halfIn), .en(mon_setLeast), .Q(register_2_q), .clk(clk), .clr(rst));
  Decoder_part #(.select(4), .disabled(0)) decoder_1 (
    .out1(decoder_1_out1), .out2(decoder_1_out2), .out3(decoder_1_out3), .out4(decoder_1_out4),
    .out5(decoder_1_out5), .out6(decoder_1_out6), .out7(decoder_1_out7), .out8(decoder_1_out8),
    .out9(decoder_1_out9), .out10(decoder_1_out10), .out11(decoder_1_out11), .out12(decoder_1_out12),
    .out13(decoder_1_out13), .out14(decoder_1_out14), .out15(decoder_1_out15), .sel(mon_inxCol), .en(mon_enIn));  // open: out0
  Register #(.width(15), .trigger("falling")) register_3 (
    .D({register_1_q[6:0], register_2_q}), .en(decoder_1_out1), .Q(out_8), .clk(clk), .clr(rst));
  Register #(.width(15), .trigger("falling")) register_4 (
    .D({register_1_q[6:0], register_2_q}), .en(decoder_1_out2), .Q(out_9), .clk(clk), .clr(rst));
  Register #(.width(15), .trigger("falling")) register_5 (
    .D({register_1_q[6:0], register_2_q}), .en(decoder_1_out3), .Q(out_10), .clk(clk), .clr(rst));
  Register #(.width(15), .trigger("falling")) register_6 (
    .D({register_1_q[6:0], register_2_q}), .en(decoder_1_out4), .Q(out_11), .clk(clk), .clr(rst));
  Register #(.width(15), .trigger("falling")) register_7 (
    .D({register_1_q[6:0], register_2_q}), .en(decoder_1_out5), .Q(out_12), .clk(clk), .clr(rst));
  Register #(.width(15), .trigger("falling")) register_8 (
    .D({register_1_q[6:0], register_2_q}), .en(decoder_1_out6), .Q(out_13), .clk(clk), .clr(rst));
  Register #(.width(15), .trigger("falling")) register_9 (
    .D({register_1_q[6:0], register_2_q}), .en(decoder_1_out7), .Q(out_14), .clk(clk), .clr(rst));
  Register #(.width(15), .trigger("falling")) register_10 (
    .D({register_1_q[6:0], register_2_q}), .en(decoder_1_out8), .Q(out_15), .clk(clk), .clr(rst));
  Register #(.width(15), .trigger("falling")) register_11 (
    .D({register_1_q[6:0], register_2_q}), .en(decoder_1_out9), .Q(out_16), .clk(clk), .clr(rst));
  Register #(.width(15), .trigger("falling")) register_12 (
    .D({register_1_q[6:0], register_2_q}), .en(decoder_1_out10), .Q(out_17), .clk(clk), .clr(rst));
  Register #(.width(15), .trigger("falling")) register_13 (
    .D({register_1_q[6:0], register_2_q}), .en(decoder_1_out11), .Q(out_18), .clk(clk), .clr(rst));
  Register #(.width(15), .trigger("falling")) register_14 (
    .D({register_1_q[6:0], register_2_q}), .en(decoder_1_out12), .Q(out_19), .clk(clk), .clr(rst));
  Register #(.width(15), .trigger("falling")) register_15 (
    .D({register_1_q[6:0], register_2_q}), .en(decoder_1_out13), .Q(out_20), .clk(clk), .clr(rst));
  Register #(.width(15), .trigger("falling")) register_16 (
    .D({register_1_q[6:0], register_2_q}), .en(decoder_1_out14), .Q(out_21), .clk(clk), .clr(rst));
  Register #(.width(15), .trigger("falling")) register_17 (
    .D({register_1_q[6:0], register_2_q}), .en(decoder_1_out15), .Q(out_22), .clk(clk), .clr(rst));
endmodule

module joystick_control (
  input  [7:0] joy_in,
  input  joy_enOut,
  output [7:0] joy_out
);

  assign joy_out = joy_enOut ? joy_in : 8'bz;  // Controlled_Buffer controlled_buffer_1
endmodule
